# Fritzing sketch ESP32_+_RPi4b (saved by Fritzing 0.8.7b)
breadboards: 3

parts:
  U1 = ESP32-38PinWide [part_number=ESP32-38PinWide]
  Mod1 = Raspberry Pi 4B
  R1 = Resistor [tolerance=±1% resistance=220 package=THT]
  R2 = Resistor [tolerance=±1% resistance=220 package=THT]
  R3 = Resistor [tolerance=±1% resistance=220 package=THT]
  R4 = Resistor [tolerance=±1% resistance=220 package=THT]
  R5 = Resistor [tolerance=±1% resistance=220 package=THT]
  R6 = Photocell (LDR) [package=THT]
  C1 = Electrolytic Capacitor [capacitance=1µF package="100 mil [THT, electrolytic]"]
  LED1 = LED - 5mm [color="Blue (430nm)" package="5 mm [THT]"]
  LED2 = LED - 5mm [color="Red (633nm)" package="5 mm [THT]"]
  LED3 = LED - 5mm [color="Yellow (595nm)" package="5 mm [THT]"]
  LED4 = LED - 5mm [color="Red (633nm)" package="5 mm [THT]"]
  LED5 = LED - 5mm [color="Green (555nm)" package="5 mm [THT]"]
  J1 = Basic Servo
  J2 = Basic Servo
  OLED_I2C1 = OLED 128x64 I2C Monochrome Display
  R7 = Resistor [tolerance=±1% resistance=220 package=THT]
  LED6 = LED - 5mm [color="White (4500K)" package="5 mm [THT]"]
  LED7 = LED - 5mm [color="White (4500K)" package="5 mm [THT]"]
  DHT1 = DHT11 Humitidy and Temperature Sensor
  YwRobot_Power_Supply1 = YwRobot Breadboard Power Supply [part_number=545043]
  Part1 = FC-28 Soil Hygrometer Module
  Part2 = FC-28 Soil Hygrometer Module - Probe
  Part3 = FC-28 Soil Hygrometer Module
  YL-83_-_Detection_Board1 = YL-83 Rain Sensor - Detection Board

nets:
  N1: U1.3.3, OLED_I2C1.VDD
  N2: U1.GPIO26, DHT1.DATA
  GND: U1.GND, OLED_I2C1.GND, R7.Pin_0, DHT1.GND, YwRobot_Power_Supply1.GND#11, YwRobot_Power_Supply1.GND#12, Part1.GND, Part3.GND
  N3: U1.GPIO4, LED6.anode, LED7.anode
  N4: U1.GPIO21, OLED_I2C1.SDA
  N5: U1.GPIO22, OLED_I2C1.SCK
  N6: Mod1.3V3, R6.pin_0
  VCC: Mod1.5V, J1.vcc, J2.vcc
  GND_2: Mod1.GND, Mod1.GPIO27, Mod1.GPIO7, Mod1.GPIO5, Mod1.GPIO21, R1.Pin_1, R2.Pin_1, R3.Pin_1, R4.Pin_1, R5.Pin_0, C1.+, LED2.cathode, LED3.cathode, LED4.anode, J1.gnd, J2.gnd
  N7: Mod1.GPIO17, Mod1.GPIO18, LED5.anode
  N8: Mod1.GPIO13, R6.pin_1, C1.-
  N9: Mod1.GPIO19, Mod1.GPIO16, LED1.cathode
  N10: R1.Pin_0, LED1.anode
  N11: R2.Pin_0, LED2.anode
  N12: R3.Pin_0, LED3.anode
  N13: R4.Pin_0, LED5.cathode
  N14: R5.Pin_1, LED4.cathode
  N15: R7.Pin_1, LED6.cathode, LED7.cathode
  VCC_2: DHT1.VDD, YwRobot_Power_Supply1.VCC#5, YwRobot_Power_Supply1.VCC#6, Part1.VCC, Part3.VCC
  N16: YwRobot_Power_Supply1.VCC#9, YwRobot_Power_Supply1.VCC#10
  N17: YwRobot_Power_Supply1.GND#13, YwRobot_Power_Supply1.GND#14
  N18: Part1.POS, Part2.POS
  N19: Part1.NEG, Part2.NEG
  N20: Part3.POS, YL-83_-_Detection_Board1.POS
  N21: Part3.NEG, YL-83_-_Detection_Board1.NEG

custom parts:
  ESP32-38PinWide: Generic 38-Pin ESP32 with wide format (only access to one side of pins on a breadboard) based on Stephen Lilley's HiLetgo ESP-WROOM-32 ESP32 ESP-32S Development Board.
  DHT11 Humitidy and Temperature Sensor: DHT11 Humidity and Temperature Sensor
  YwRobot Breadboard Power Supply: The YwRobot Breadboard Power Supply (MB-V2) has two power rails; they can be 5V or 3V3. Power to the module can be provided through the female USB socket or through the A10 (female) 2.1mm power jack.
  FC-28 Soil Hygrometer Module: The FC-28 is a soil hygrometer module that uses the Texas Instruments LM393 comparator chip to provide an analog measurement of soil humidity. The digital output is high when soil moisture is over a certain threshold, as determined by adjusting the potentiometer.
  FC-28 Soil Hygrometer Module - Probe: The FC-28 is a soil hygrometer module that uses the Texas Instruments LM393 comparator chip to provide an analog measurement of soil humidity.
  YL-83 Rain Sensor - Detection Board: The YL-83 is a rain sensor that has more resistance when dry and less resistance when wet. The module runs at 5V.
